// Logisim project odvdn10_logisim.circ as structural Verilog: 3 circuits, main circuit main
module main (
  input  x1,
  input  x2
);

  wire clock_1_out, sr1_1_r1, sr1_1_s1, sr2_1_r2, sr2_1_s2;
  wire [1:0] s_r_ff_2_q;

  Clock clock_1 (.out(clock_1_out));
  sr1 sr1_1 (.q1(s_r_ff_2_q[1]), .q2(s_r_ff_2_q[0]), .x1(x1), .x2(x2), .s1(sr1_1_s1), .r1(sr1_1_r1));
  sr2 sr2_1 (.q1(s_r_ff_2_q[1]), .q2(s_r_ff_2_q[0]), .x1(x1), .x2(x2), .s2(sr2_1_s2), .r2(sr2_1_r2));
  S_R_Flip_Flop s_r_ff_1 (
    .S(sr1_1_s1), .clk(clock_1_out), .R(sr1_1_r1), .Q(s_r_ff_2_q[1]));  // open: Qn, preset, reset, en
  S_R_Flip_Flop s_r_ff_2 (
    .S(sr2_1_s2), .clk(clock_1_out), .R(sr2_1_r2), .Q(s_r_ff_2_q[0]));  // open: Qn, preset, reset, en
  Hex_Digit_Display hex_digit_display_1 (.value({2'b00, s_r_ff_2_q}));  // open: dp
endmodule

module sr1 (
  input  q1,
  input  q2,
  input  x1,
  input  x2,
  output s1,
  output r1
);

  wire and_1_out, and_2_out, and_3_out, and_4_out, and_5_out, not_1_out, not_2_out, not_3_out, not_4_out;

  not not_1 (not_1_out, q1);
  not not_2 (not_2_out, q2);
  not not_3 (not_3_out, x1);
  not not_4 (not_4_out, x2);
  and and_1 (and_1_out, x1, x2, not_1_out, not_2_out);
  and and_2 (and_2_out, x1, not_4_out, q2, not_1_out);
  and and_3 (and_3_out, q1, not_3_out, not_4_out);
  and and_4 (and_4_out, x1, x2, q1, not_2_out);
  and and_5 (and_5_out, x1, not_4_out, q1, q2);
  or or_1 (s1, and_1_out, and_2_out);
  or or_2 (r1, and_3_out, and_4_out, and_5_out);
endmodule

module sr2 (
  input  q1,
  input  q2,
  input  x1,
  input  x2,
  output s2,
  output r2
);

  wire and_1_out, and_2_out, not_1_out, not_2_out, not_3_out, not_4_out;

  not not_1 (not_1_out, q1);
  not not_2 (not_2_out, q2);
  not not_3 (not_3_out, x1);
  not not_4 (not_4_out, x2);
  and and_1 (and_1_out, not_4_out, q2);
  or or_1 (r2, and_1_out, and_2_out);
  and and_2 (and_2_out, x1, x2, q2);
  and and_3 (s2, x1, not_2_out);
endmodule
